// Logisim project projeto3.circ as structural Verilog: 2 circuits, main circuit main
module main (
);

  RegistBank registbank_1 ();  // open: setValue, WriteE, R, RegistoN, ReadOut
endmodule

// NRegisto
module RegistBank (
  input  [15:0] setValue,
  input  WriteE,
  input  R,
  input  [2:0] RegistoN,
  output [15:0] ReadOut
);

  wire decoder_1_out0, decoder_1_out1, decoder_1_out2, decoder_1_out3, decoder_1_out4, decoder_1_out5,
       decoder_1_out6, decoder_1_out7;
  wire [15:0] register_1_q, register_2_q, register_3_q, register_4_q, register_5_q, register_6_q,
       register_7_q, register_8_q;

  Decoder #(.select(3)) decoder_1 (
    .out0(decoder_1_out0), .out1(decoder_1_out1), .out2(decoder_1_out2), .out3(decoder_1_out3),
    .out4(decoder_1_out4), .out5(decoder_1_out5), .out6(decoder_1_out6), .out7(decoder_1_out7),
    .sel(RegistoN), .en(WriteE));
  Register #(.width(16)) register_1 (.D(setValue), .en(decoder_1_out0), .clk(R), .Q(register_1_q));  // open: clr
  Register #(.width(16)) register_2 (.D(setValue), .en(decoder_1_out1), .clk(R), .Q(register_2_q));  // open: clr
  Register #(.width(16)) register_3 (.D(setValue), .en(decoder_1_out2), .clk(R), .Q(register_3_q));  // open: clr
  Register #(.width(16)) register_4 (.D(setValue), .en(decoder_1_out3), .clk(R), .Q(register_4_q));  // open: clr
  Register #(.width(16)) register_5 (.D(setValue), .en(decoder_1_out4), .clk(R), .Q(register_5_q));  // open: clr
  Register #(.width(16)) register_6 (.D(setValue), .en(decoder_1_out5), .clk(R), .Q(register_6_q));  // open: clr
  Register #(.width(16)) register_7 (.D(setValue), .en(decoder_1_out6), .clk(R), .Q(register_7_q));  // open: clr
  Register #(.width(16)) register_8 (.D(setValue), .en(decoder_1_out7), .clk(R), .Q(register_8_q));  // open: clr
  Multiplexer #(.select(3), .width(16)) multiplexer_1 (
    .in0(register_1_q), .in1(register_2_q), .in2(register_3_q), .in3(register_4_q), .in4(register_5_q),
    .in5(register_6_q), .in6(register_7_q), .in7(register_8_q), .out(ReadOut), .sel(RegistoN));
endmodule
